# Fritzing sketch schemaReader (saved by Fritzing 0.9.3b)

parts:
  Componente1 = Real Time Clock Module - DS1307 RTC Breakout Board [part_number="RTC ds1307"]
  Componente2 = Arduino Mega ADK (Rev3)
  Componente3 = Arduino Ethernet Shield (Rev3)
  LCD2 = LCD screen [part_number="LCD 20x4"]
  Grove1 = Grove Speaker [part_number="Grove Speaker"]
  Componente4 = RFID-RC522-v2 [part_number="Rfid RC522"]
  SPKR1 = Loudspeaker [part_number=" 8 Ohm"]
  R1 = Resistor [tolerance=±5% resistance=470 part_number=R1 package=THT]
  R2 = Resistor [tolerance=±5% resistance=470 part_number=R2 package=THT]
  R3 = Resistor [tolerance=±5% resistance=470 package=THT]
  R4 = Resistor [tolerance=±5% resistance=470 package=THT]
  LED3 = LED - 5mm [color="White (4500K)" package="5 mm [THT]"]  # not connected
  LED4 = LED - 5mm [color="White (4500K)" package="5 mm [THT]"]  # not connected
  LED1 = LED - 5mm [color="White (4500K)" package="5 mm [THT]"]  # not connected
  LED2 = LED - 5mm [color="White (4500K)" package="5 mm [THT]"]
  Sw1 = Round Pushbutton
  R5 = Resistor [tolerance=±5% resistance=10k package=THT]
  C1 = Electrolytic Capacitor [capacitance=0.47mF voltage=20V package="100 mil [THT, electrolytic]"]
  R6 = Resistor [tolerance=±5% resistance=22k package=THT]

nets:
  5V: Componente1.5V, Componente3.5V, LCD2.VDD, LED2.anode, R6.Pin_1
  GND: Componente1.GND, Componente3.GND, LCD2.VSS, Grove1.GND, Componente4.GND
  N1: Componente1.SQW, Componente3.D2
  N2: Componente1.SCL, Componente2.D21/SCL
  N3: Componente1.SDA, Componente2.D20/SDA
  N4: Componente2.D17/RX2, LCD2.DB4
  N5: Componente2.D16/TX2, LCD2.DB5
  N6: Componente2.D15/RX3, LCD2.DB6
  N7: Componente2.D14/TX3, LCD2.DB7
  N8: Componente2.D31, R1.Pin_0
  N9: Componente2.D33, R2.Pin_0
  N10: Componente2.D34, C1.-
  N11: Componente2.D35, R3.Pin_0
  N12: Componente2.D37, R4.Pin_0
  N13: Componente2.D40, Sw1.leg0
  N14: Componente2.D46, Grove1.SIG
  N15: Componente2.D48, Componente4.RST
  N16: Componente2.D50/MISO, Componente4.MISO
  N17: Componente2.D51/MOSI, Componente4.MOSI
  N18: Componente2.D52/SCK, Componente4.SCK
  N19: Componente2.D53/SS, Componente4.SDA
  N20: Componente2.GND, R5.Pin_1
  N21: Componente3.D8, LCD2.RS
  N22: Componente3.PWM_D9, LCD2.E
  3V3: Componente3.3V3, Componente4.3.3V
  N23: Grove1.pin_+, SPKR1.pin2
  N24: Grove1.pin_-, SPKR1.pin1

notes:
  led high intensity

custom parts:
  LCD screen: A standard character display, usually with 2x16 characters. Comes in many colors.
  Grove Speaker: audio amplifier
  RFID-RC522-v2: A simple China made RFID-RC522 Reader; do check the pin labels, as this is a MFRC522 based clone.
